# Fritzing sketch esp32cam-sd-i2s (saved by Fritzing 0.9.6b)

parts:
  Power_plug_3_6V1 = Power plug [part_number="Vcc +5V"]
  J3 = single row smd male pin header, 6 pins [form="♂ (male)"]
  Q1 = NPN-Transistor [package="TO92 [THT]"]
  Q2 = NPN-Transistor [package="TO92 [THT]"]
  R14 = Resistor [tolerance=±10% resistance=15k power=0.25 package=THT]
  R15 = Resistor [tolerance=±10% resistance=15k power=0.25 package=THT]
  J4 = single row smd male pin header, 6 pins [form="♂ (male)"]
  ESP32_-_Back1 = ESP32 - CAM
  J5 = single row smd male pin header, 6 pins [form="♂ (male)" part_number="To the programmer"]
  SPKR2 = Loudspeaker  # not connected
  Part2 = Adafruit MAX98357A I2S 3W Class D Amplifier [part_number="Adafruit #3006"]
  J6 = single row smd male pin header, 3 pins [form="♂ (male)"]
  M4 = Dagu DGServo 9g (Top view) [part_number=RS001B]
  M5 = Dagu DGServo 9g (Top view) [part_number=RS001B]
  M6 = Dagu DGServo 9g (Top view) [part_number=RS001B]
  C2 = Electrolytic Capacitor [capacitance=0.47mF voltage=35V package="0807 [SMD, electrolytic]"]

nets:
  N1: Power_plug_3_6V1.GND, J3.pin2, ESP32_-_Back1.GND#12, J5.pin2
  VCC: Power_plug_3_6V1.VCC, J3.pin1, ESP32_-_Back1.5V, J5.pin1, Part2.VIN, M4.vcc, C2.+
  N2: J3.pin3, J4.pin3, ESP32_-_Back1.GPIO3_/_RX, J5.pin3
  N3: J3.pin4, J4.pin4, ESP32_-_Back1.GPIO1_/_TX, J5.pin4
  N4: J3.pin5, Q1.C, J5.pin5
  N5: J3.pin6, Q2.C, ESP32_-_Back1.GPIO0, J5.pin6
  N6: Q1.E, R15.Pin_1, J4.pin5
  N7: Q1.B, R14.Pin_0
  N8: Q2.E, R14.Pin_1, J4.pin6
  N9: Q2.B, R15.Pin_0
  GND: ESP32_-_Back1.GND#7, Part2.GND, M4.gnd, M5.gnd, C2.-
  N10: Part2.DIN, J6.pin1
  N11: Part2.BCLK, J6.pin2
  N12: Part2.LRCLK, J6.pin3
  VCC_2: M5.vcc, M6.vcc

notes:
  Vcc + 5V
  GND
  RXD < -------- TXD
  TXD -----------> RXD
  EN/RST
  IO0/FLASH
  GND
  TXD
  RXD
  RTS
  DTR
  Reset and Flash by RTS and DTR
  DIN - GPIO 21
  BCLK-GPIO 22->23
  LRC - GPIO 23->22
  Bell01 GPIO 25
  Bell23 GPIO 26
  Bell45 GPIO 27

custom parts:
  ESP32 - CAM: The ESP32-CAM has a very competitive small-size camera module that can operate independently as a minimum system with a footprint of only 27*40.5*4.5mm and a deep sleep current of up to 6mA.
  Adafruit MAX98357A I2S 3W Class D Amplifier: Listen to this good news - we now have an all in one digital audio amp breakout board that works incredibly well with the Raspberry Pi! If you're looking for an easy and low cost way to get you digital sound files bumpin' then the MAX08357 I2S Amp Breakout is for you. It takes standard I2S digital audio input and, not only decodes it into analog, but also amplifies it directly into a speaker.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
